# Fritzing sketch door (saved by Fritzing 0.9.3b)
circuit board: 15.6374cm x 8.91002cm
perfboards: 1

parts:
  U2 = 2-Channel 5v Relay Shield [package=relay-2ch5v10a]
  S2 = Pushbutton [package=THT]
  Part3 = Arduino Wireless SD Shield
  Part2 = RFID-RC522-v2

nets (from the pcb view):
  VCC: U2.VCC, S2.leg0, Part3.+5V
  GND: U2.GND, Part3.GND, Part2.GND
  N1: U2.IN1, Part3.D2
  N2: S2.leg1, Part3.D3
  N3: Part3.D8, Part2.RST
  N4: Part3.SD_CS, Part2.SDA
  N5: Part3.D5, Part2.SCK
  N6: Part3.D6, Part2.MISO
  N7: Part3.D7, Part2.MOSI
  3.3V: Part3.3.3V, Part2.3.3V

custom parts:
  2-Channel 5v Relay Shield: 2 Channel 5v Relay Shield w. 2x SPD-06VDC-SD-C
  RFID-RC522-v2: A simple China made RFID-RC522 Reader; do check the pin labels, as this is a MFRC522 based clone.
